# Fritzing sketch Theremin LDR (saved by Fritzing 0.9.3b)
breadboards: 1

parts:
  Componente1 = Arduino Uno (Rev3)
  R1 = Photocell (LDR) [package=THT]
  R2 = Resistor [tolerance=±5% resistance=10k package="0402 [SMD]"]
  SP1 = SPEAKER [package=pcb_mount_speaker]

nets:
  N1: Componente1.A0, R1.pin_0, R2.Pin_1
  N2: Componente1.D11_PWM/MOSI, SP1.-
  N3: Componente1.5V, R2.Pin_0
  N4: Componente1.GND, R1.pin_1, SP1.+
